// Logisim project circuits.circ as structural Verilog
module X (
  input  A,
  input  B,
  input  C,
  output X1,
  output X2,
  output X3,
  output X4,
  output X5,
  output X6,
  output X7,
  output X8
);

  circuit_X1 circuit_x1_1 (.A(A), .B(B), .X1(X1));
  circuit_X2 circuit_x2_1 (.A(A), .B(B), .C(C), .X2(X2));
  circuit_X3 circuit_x3_1 (.A(A), .B(B), .C(C), .X3(X3));
  circuit_X4 circuit_x4_1 (.A(A), .B(B), .C(C), .X4(X4));
  circuit_X5 circuit_x5_1 (.A(A), .B(B), .C(C), .X5(X5));
  circuit_X6 circuit_x6_1 (.A(A), .B(B), .X6(X6));
  circuit_X7 circuit_x7_1 (.A(A), .B(B), .C(C), .X7(X7));
  circuit_X8 circuit_x8_1 (.A(A), .B(B), .X8(X8));
endmodule

module circuit_X1 (
  input  A,
  input  B,
  output X1
);

  wire and_1_out, nor_1_out, not_1_out, not_2_out, or_1_out;

  not not_1 (not_1_out, A);
  not not_2 (not_2_out, B);
  and and_1 (and_1_out, A, not_2_out);
  or or_1 (or_1_out, and_1_out, not_1_out);
  nor nor_1 (nor_1_out, A, not_2_out);
  and and_2 (X1, or_1_out, B, nor_1_out);
endmodule

module circuit_X2 (
  input  A,
  input  B,
  input  C,
  output X2
);

  wire and_1_out, and_2_out, and_3_out, nand_1_out, not_1_out, not_2_out, not_3_out, or_1_out, or_2_out;

  not not_1 (not_1_out, A);
  not not_2 (not_2_out, C);
  not not_3 (not_3_out, B);
  and and_1 (and_1_out, A, B);
  or or_1 (or_1_out, and_1_out, not_1_out);
  and and_2 (and_2_out, B, not_2_out);
  nand nand_1 (nand_1_out, or_1_out, C);
  or or_2 (or_2_out, and_2_out, A);
  and and_3 (and_3_out, or_2_out, not_3_out);
  or or_3 (X2, nand_1_out, and_3_out);
endmodule

module circuit_X3 (
  input  A,
  input  B,
  input  C,
  output X3
);

  wire not_1_out, not_2_out, or_1_out, or_2_out, or_3_out;

  not not_1 (not_1_out, A);
  not not_2 (not_2_out, C);
  or or_1 (or_1_out, A, B);
  or or_2 (or_2_out, B, C);
  or or_3 (or_3_out, not_1_out, not_2_out);
  and and_1 (X3, or_1_out, or_2_out, or_3_out);
endmodule

module circuit_X4 (
  input  A,
  input  B,
  input  C,
  output X4
);

  wire and_1_out, and_2_out, nor_1_out, not_1_out, not_2_out, not_3_out, or_1_out, or_2_out;

  not not_1 (not_1_out, A);
  not not_2 (not_2_out, B);
  not not_3 (not_3_out, C);
  and and_1 (and_1_out, A, B);
  and and_2 (and_2_out, A, not_2_out);
  nor nor_1 (nor_1_out, not_1_out, C);
  or or_1 (or_1_out, and_1_out, B);
  or or_2 (or_2_out, and_2_out, nor_1_out);
  and and_3 (X4, or_1_out, not_3_out, or_2_out);
endmodule

module circuit_X5 (
  input  A,
  input  B,
  input  C,
  output X5
);

  wire and_1_out, nand_1_out, nand_2_out, not_1_out, not_2_out, not_3_out, or_1_out, or_2_out, or_3_out,
       or_4_out;

  not not_1 (not_1_out, A);
  and and_1 (and_1_out, not_1_out, C);
  not not_2 (not_2_out, B);
  not not_3 (not_3_out, C);
  or or_1 (or_1_out, A, B);
  or or_2 (or_2_out, and_1_out, not_2_out);
  nand nand_1 (nand_1_out, or_1_out, or_2_out);
  or or_3 (or_3_out, A, not_2_out);
  or or_4 (or_4_out, nand_1_out, B);
  nand nand_2 (nand_2_out, or_3_out, not_3_out);
  and and_2 (X5, or_4_out, nand_2_out);
endmodule

module circuit_X6 (
  input  A,
  input  B,
  output X6
);

  wire not_1_out;

  not not_1 (not_1_out, A);
  ExactlyOne xor_1 (.out(X6), .in0(A), .in1(B), .in2(not_1_out));
endmodule

module circuit_X7 (
  input  A,
  input  B,
  input  C,
  output X7
);

  wire and_1_out, or_1_out, xnor_1_out, xor_1_out;

  and and_1 (and_1_out, A, xor_1_out);
  xor xor_1 (xor_1_out, B, C);
  or or_1 (or_1_out, and_1_out, ~A);  // OR_Gate
  xnor xnor_1 (xnor_1_out, B, C);
  and and_2 (X7, or_1_out, xnor_1_out);
endmodule

module circuit_X8 (
  input  A,
  input  B,
  output X8
);

  wire and_1_out, xnor_1_out, xor_1_out, xor_2_out;

  xor xor_1 (xor_1_out, A, B);
  xor xor_2 (xor_2_out, A, ~B);  // XOR_Gate
  and and_1 (and_1_out, xor_1_out, xor_2_out);
  xnor xnor_1 (xnor_1_out, ~A, B);  // XNOR_Gate
  or or_1 (X8, and_1_out, xnor_1_out);
endmodule
