// Logisim project norm_template.circ as structural Verilog: 10 circuits, main circuit main
module main (
  input  [31:0] in_1,
  input  [31:0] in_2,
  input  [27:0] in_3,
  input  [27:0] in_4,
  output [27:0] out_5,
  output [27:0] out_6,
  output [27:0] out_7
);

  wire button_1_out, button_2_out, clock_1_out, clock_2_out, norm_1_done, norm_2_done;
  wire [27:0] norm_1_debug_x, norm_1_debug_y, norm_1_outp, q12_16_fromfloat_1_q, q12_16_fromfloat_2_q;
  wire [31:0] q12_16_tofloat_1_f, q12_16_tofloat_2_f, q12_16_tofloat_3_f;

  Button button_1 (.out(button_1_out));
  Button button_2 (.out(button_2_out));
  // Probe on q12_16_fromfloat_1_q
  // Probe on q12_16_fromfloat_2_q
  Q12_16_fromfloat q12_16_fromfloat_1 (.F(in_1), .Q(q12_16_fromfloat_1_q));
  Q12_16_fromfloat q12_16_fromfloat_2 (.F(in_2), .Q(q12_16_fromfloat_2_q));
  Clock clock_1 (.out(clock_1_out));
  Clock clock_2 (.out(clock_2_out));
  NORM norm_1 (
    .X_IN(q12_16_fromfloat_1_q), .Y_IN(q12_16_fromfloat_2_q), .START(button_1_out), .CLK(clock_1_out),
    .OUTP(norm_1_outp), .DONE(norm_1_done), .DEBUG_X(norm_1_debug_x), .DEBUG_Y(norm_1_debug_y));
  LED led_1 (.in(norm_1_done));
  NORM norm_2 (
    .X_IN(in_3), .Y_IN(in_4), .START(button_2_out), .CLK(clock_2_out), .OUTP(out_5), .DONE(norm_2_done),
    .DEBUG_X(out_6), .DEBUG_Y(out_7));
  LED led_2 (.in(norm_2_done));
  // Probe on norm_1_outp
  // Probe on q12_16_tofloat_1_f
  Q12_16_tofloat q12_16_tofloat_1 (.Q(norm_1_outp), .F(q12_16_tofloat_1_f));
  // Probe on q12_16_tofloat_2_f
  Q12_16_tofloat q12_16_tofloat_2 (.Q(norm_1_debug_x), .F(q12_16_tofloat_2_f));
  // Probe on q12_16_tofloat_3_f
  Q12_16_tofloat q12_16_tofloat_3 (.Q(norm_1_debug_y), .F(q12_16_tofloat_3_f));

  // Notes on the sheet:
  //   Pokud naimplementujete modul přesně jako já, dostanete identickou hodnotu
  //   Ale nějaká drobná odchylka (jak od správného výsledku, tak od mojí implementace) je povolitelná
  //   V tomto modulu nic neupravujte, kromě hodnot.
  //   Na konečné testování si můžete zapnout "Auto-Tick" a zvýšit frekvenci
  //   Testování pomocí float inputů a outputů (pro vaše zhruba testování)
  //   Testování pomocí konkrétních Q12.16 hodnot (pro poskytnuté testovací vektory)
  //   Pokud modul NORM nefunguje v tomto modulu, nebude fungovat v opravovači!
endmodule

module NORM (
  input  [27:0] X_IN,
  input  [27:0] Y_IN,
  input  START,
  input  CLK,
  output [27:0] OUTP,
  output DONE,
  output [27:0] DEBUG_X,
  output [27:0] DEBUG_Y
);

  Multiplier #(.width(28)) multiplier_1 ();  // open: a, b, out, cin, cout
  // ADDSUB addsub_1: pin names not known
  // ADDSUB addsub_2: pin names not known

  // Other names for the same wires on the sheet: DX[27:0] = DEBUG_X; DY[27:0] = DEBUG_Y
endmodule

module ADDSUB (
  input  [27:0] A,
  input  [27:0] B,
  input  SUB,
  output [27:0] OUTP
);

  wire [27:0] multiplexer_1_out, not_1_out;

  assign not_1_out = ~B;  // NOT_Gate not_1, 28 bits wide
  Multiplexer #(.width(28)) multiplexer_1 (.in0(B), .in1(not_1_out), .out(multiplexer_1_out), .sel(SUB));
  Adder #(.width(28)) adder_1 (.a(A), .b(multiplexer_1_out), .out(OUTP), .cin(SUB));  // open: cout
endmodule

module Q12_16_tofloat (
  input  [27:0] Q,
  output [31:0] F
);

  wire [31:0] inttofp_1_p2;

  // IntToFP #(.width(28)) inttofp_1: pin names not known; wires that end beside it: Q, inttofp_1_p2
  // Probe on F
  FPMultiplier fpmultiplier_1 (.a(inttofp_1_p2), .b(32'h37800000), .out(F));

  // Notes on the sheet:
  //   2^-16
  //   na výstup modulu si dejte "probe" s radixem "float"
endmodule

module Q12_16_tofloat_tutorial (
);

  wire [31:0] q12_16_tofloat_1_f;

  Q12_16_tofloat q12_16_tofloat_1 (.Q(28'h3243f), .F(q12_16_tofloat_1_f));
  // Probe on q12_16_tofloat_1_f

  // Notes on the sheet:
  //   nejbližší číslo k "pi" v Q12.16
  //   to samé číslo jako float
endmodule

module Q12_16_fromfloat (
  input  [31:0] F,
  output [27:0] Q
);

  wire [31:0] fpmultiplier_1_out;

  FPMultiplier fpmultiplier_1 (.a(F), .b(32'h47800000), .out(fpmultiplier_1_out));
  // FPToInt #(.width(28)) fptoint_1: pin names not known; wires that end beside it: fpmultiplier_1_out, Q

  // Notes on the sheet:
  //   2^16
endmodule

module NORM_GOLDEN (
  input  [27:0] X_IN,
  input  [27:0] Y_IN,
  output [27:0] OUTP
);

  wire fpsquareroot_1_p2;
  wire [31:0] fptofp_3_p2, q12_16_tofloat_1_f, q12_16_tofloat_2_f;
  wire [63:0] fpadder_1_out, fpmultiplier_1_out, fpmultiplier_2_out, fptofp_1_p2, fptofp_2_p2;

  // Probe on q12_16_tofloat_1_f
  Q12_16_tofloat q12_16_tofloat_1 (.Q(X_IN), .F(q12_16_tofloat_1_f));
  // Probe on q12_16_tofloat_2_f
  Q12_16_tofloat q12_16_tofloat_2 (.Q(Y_IN), .F(q12_16_tofloat_2_f));
  // FPToFP #(.fpwidthout(64)) fptofp_1: pin names not known; wires that end beside it: q12_16_tofloat_1_f, fptofp_1_p2
  // FPToFP #(.fpwidthout(64)) fptofp_2: pin names not known; wires that end beside it: q12_16_tofloat_2_f, fptofp_2_p2
  // Probe on fpmultiplier_1_out
  FPMultiplier #(.fpwidth(64)) fpmultiplier_1 (.a(fptofp_1_p2), .b(fptofp_1_p2), .out(fpmultiplier_1_out));
  // Probe on fpmultiplier_2_out
  FPMultiplier #(.fpwidth(64)) fpmultiplier_2 (.a(fptofp_2_p2), .b(fptofp_2_p2), .out(fpmultiplier_2_out));
  // Probe on fpadder_1_out
  FPAdder #(.fpwidth(64)) fpadder_1 (.a(fpmultiplier_1_out), .b(fpmultiplier_2_out), .out(fpadder_1_out));
  // FPSquareRoot #(.fpwidth(64)) fpsquareroot_1: pin names not known; wires that end beside it: fpadder_1_out, fpsquareroot_1_p2
  // Probe on fpsquareroot_1_p2
  // FPToFP #(.fpwidthin(64)) fptofp_3: pin names not known; wires that end beside it: fpsquareroot_1_p2, fptofp_3_p2
  Q12_16_fromfloat q12_16_fromfloat_1 (.F(fptofp_3_p2), .Q(OUTP));

  // Notes on the sheet:
  //   Implementace normy podle vzorce pomocí Logisimových FP komponent
  //   Lze použít jako "Golden Standard" - víme, že počítá správně, můžeme porovnávat
endmodule

module NORM_GOLDEN_TEST (
  input  [27:0] X_IN,
  input  [27:0] Y_IN,
  input  START,
  input  CLK,
  output PASS,
  output FAIL,
  output TIMEOUT,
  output DONE,
  output [27:0] DX,
  output [27:0] DY,
  output [27:0] OUTP_ACTUAL,
  output [27:0] OUTP_EXPECTED
);

  wire absolute_1_p2, accurate, and_6_out, comparator_4_lt, comparator_5_gt, d_ff_1_q, dut_done, dut_start,
       not_1_out, or_1_out, or_2_out, or_3_out, stop, zero;
  wire [7:0] adder_1_out, multiplexer_1_out, register_3_q;
  wire [27:0] absolute_2_p2, DY_t, multiplexer_2_out, multiplexer_3_out, random_1_out, random_2_out,
       subtractor_1_out;
  wire [31:0] fpdivider_1_out, fpmultiplier_1_out, fptoint_1_p2, inttofp_1_p1, inttofp_2_p1, max_error_q,
       q12_16_tofloat_1_f, q12_16_tofloat_2_f;

  Register #(.width(28)) register_1 (.D(X_IN), .en(START), .clk(CLK), .Q(DX));  // open: clr
  Register #(.width(28)) register_2 (.D(Y_IN), .en(START), .clk(CLK), .Q(DY_t));  // open: clr
  Multiplexer #(.width(8)) multiplexer_1 (.in0(adder_1_out), .in1({8{1'b0}}), .out(multiplexer_1_out), .sel(START));
  not not_1 (not_1_out, stop);
  or or_1 (or_1_out, not_1_out, START);
  Adder adder_1 (.a(8'h1), .b(register_3_q), .out(adder_1_out));  // open: cin, cout
  Register register_3 (.D(multiplexer_1_out), .en(or_1_out), .clk(CLK), .Q(register_3_q));  // open: clr
  Random #(.width(28)) random_1 (.clk(CLK), .out(random_1_out));  // open: clr, next
  Random #(.seed(1), .width(28)) random_2 (.clk(CLK), .out(random_2_out));  // open: clr, next
  Subtractor #(.width(28)) subtractor_1 (
    .a(OUTP_ACTUAL), .b(OUTP_EXPECTED), .out(subtractor_1_out));  // open: bin, bout
  // Absolute #(.width(28)) absolute_1: pin names not known; wires that end beside it: subtractor_1_out, absolute_1_p2, absolute_1_p2
  // IntToFP #(.mode("unsigned"), .width(28)) inttofp_1: pin names not known; wires that end beside it: inttofp_1_p1
  // Absolute #(.width(28)) absolute_2: pin names not known; wires that end beside it: OUTP_ACTUAL, absolute_2_p2, absolute_2_p2
  // IntToFP #(.mode("unsigned"), .width(28)) inttofp_2: pin names not known; wires that end beside it: inttofp_2_p1
  Multiplexer #(.width(28)) multiplexer_2 (.in0(random_1_out), .in1(DX), .out(multiplexer_2_out), .sel(dut_start));
  Multiplexer #(.width(28)) multiplexer_3 (.in0(random_2_out), .in1(DY_t), .out(multiplexer_3_out), .sel(dut_start));
  NORM_GOLDEN norm_golden_1 (.X_IN(DX), .Y_IN(DY_t), .OUTP(OUTP_EXPECTED));
  Comparator #(.mode("unsigned")) comparator_1 (.a(register_3_q), .b({8{1'b0}}), .eq(dut_start));  // open: gt, lt
  Comparator #(.mode("unsigned")) comparator_2 (.a(register_3_q), .b(8'h28), .eq(TIMEOUT));  // open: gt, lt
  FPDivider fpdivider_1 (.a(inttofp_1_p1), .b(inttofp_2_p1), .out(fpdivider_1_out));
  Comparator #(.mode("unsigned"), .width(28)) comparator_3 (
    .a(absolute_2_p2), .b({28{1'b0}}), .eq(zero));  // open: gt, lt
  // Probe on q12_16_tofloat_1_f
  Q12_16_tofloat q12_16_tofloat_1 (.Q(OUTP_EXPECTED), .F(q12_16_tofloat_1_f));
  FPMultiplier fpmultiplier_1 (.a(fpdivider_1_out), .b(32'h49742400), .out(fpmultiplier_1_out));
  and and_1 (PASS, DONE, ~TIMEOUT, accurate);  // AND_Gate
  // FPToInt #(.width(32)) fptoint_1: pin names not known; wires that end beside it: fpmultiplier_1_out, fptoint_1_p2
  and and_2 (FAIL, DONE, ~TIMEOUT, ~accurate);  // AND_Gate
  or or_2 (or_2_out, dut_done, TIMEOUT);
  Comparator #(.mode("unsigned"), .width(32)) comparator_4 (
    .a(fptoint_1_p2), .b(32'h64), .lt(comparator_4_lt));  // open: gt, eq
  // Probe on q12_16_tofloat_2_f
  Q12_16_tofloat q12_16_tofloat_2 (.Q(OUTP_ACTUAL), .F(q12_16_tofloat_2_f));
  NORM norm_1 (
    .X_IN(multiplexer_2_out), .Y_IN(multiplexer_3_out), .START(dut_start), .CLK(CLK), .OUTP(OUTP_ACTUAL),
    .DONE(dut_done));  // open: DEBUG_X, DEBUG_Y
  and and_3 (stop, or_2_out, ~dut_start);  // AND_Gate
  D_Flip_Flop d_ff_1 (.D(stop), .clk(CLK), .Q(d_ff_1_q));  // open: Qn, preset, reset
  and and_4 (accurate, comparator_4_lt, ~zero);  // AND_Gate
  and and_5 (DONE, stop, ~d_ff_1_q);  // AND_Gate
  Register #(.width(32)) max_error (.D(fptoint_1_p2), .en(and_6_out), .clk(CLK), .Q(max_error_q));  // open: clr
  and and_6 (and_6_out, ~zero, or_3_out, comparator_5_gt);  // AND_Gate
  or or_3 (or_3_out, PASS, FAIL);
  Comparator #(.mode("unsigned"), .width(32)) comparator_5 (
    .a(fptoint_1_p2), .b(max_error_q), .gt(comparator_5_gt));  // open: eq, lt

  assign DY = DX;

  // Notes on the sheet:
  //   Tento modul otestuje NORM proti NORM_GOLDEN s urcitou toleranci a timeoutem a reportuje vysledek
  //   timeout
  //   10^6
  //   relativni tolerance (v miliontinach)
endmodule

module NORM_TEST_BATTERY (
  output dut_pass,
  output dut_done,
  output [27:0] DX,
  output [27:0] DY,
  output [27:0] OUTP_ACTUAL,
  output [27:0] OUTP_EXPECTED,
  output [7:0] PASSES,
  output [7:0] FAILS,
  output [7:0] TIMEOUTS,
  output halt,
  output [7:0] WRONG_ADDR,
  output [27:0] WRONG_X,
  output [27:0] WRONG_Y
);

  wire and_1_out, clk, dut_start, dut_started, fail, first_wrong, next_test, s_r_ff_1_q, s_r_ff_2_q,
       s_r_ff_3_qn, tests_done, timeout, wrong, wrong_continue_out;
  wire [7:0] adder_1_out, testnr;
  wire [27:0] testx, testy;
  wire [31:0] q12_16_tofloat_1_f, q12_16_tofloat_2_f;

  Clock clock_1 (.out(clk));
  ROM #(.dataWidth(28)) Y_ROM (.addr(testnr), .data(testx));
  ROM #(.dataWidth(28)) X_ROM (.addr(testnr), .data(testy));
  Adder adder_1 (.a(8'h1), .b(testnr), .out(adder_1_out));  // open: cin, cout
  Register register_1 (.D(adder_1_out), .en(next_test), .clk(clk), .Q(testnr));  // open: clr
  Button wrong_continue (.out(wrong_continue_out));
  and and_1 (and_1_out, wrong, 1'b0);
  or or_1 (wrong, fail, timeout);
  S_R_Flip_Flop s_r_ff_1 (.S(wrong), .R(1'b0), .clk(clk), .Q(s_r_ff_1_q));  // open: reset, Qn, preset
  Comparator #(.mode("unsigned")) comparator_1 (.a(testnr), .b(8'h33), .eq(tests_done));  // open: gt, lt
  S_R_Flip_Flop s_r_ff_2 (.S(and_1_out), .R(wrong_continue_out), .clk(clk), .Q(s_r_ff_2_q));  // open: reset, Qn, preset
  S_R_Flip_Flop s_r_ff_3 (
    .S(s_r_ff_3_qn), .R(next_test), .clk(clk), .Q(dut_started), .Qn(s_r_ff_3_qn));  // open: reset, preset
  and and_2 (first_wrong, wrong, ~s_r_ff_1_q);  // AND_Gate
  and and_3 (next_test, dut_started, dut_done, ~halt);  // AND_Gate
  // Probe on q12_16_tofloat_1_f
  Q12_16_tofloat q12_16_tofloat_1 (.Q(testx), .F(q12_16_tofloat_1_f));
  // Probe on q12_16_tofloat_2_f
  Q12_16_tofloat q12_16_tofloat_2 (.Q(testy), .F(q12_16_tofloat_2_f));
  or or_2 (halt, and_1_out, s_r_ff_2_q, tests_done);
  and and_4 (dut_start, s_r_ff_3_qn, ~halt);  // AND_Gate
  NORM_GOLDEN_TEST norm_golden_test_1 (
    .X_IN(testx), .Y_IN(testy), .START(dut_start), .CLK(clk), .PASS(dut_pass), .FAIL(fail),
    .TIMEOUT(timeout), .DONE(dut_done), .DX(DX), .DY(DY), .OUTP_ACTUAL(OUTP_ACTUAL),
    .OUTP_EXPECTED(OUTP_EXPECTED));
  LED led_1 (.in(halt));
  Register WRONG_ADDR_R (.D(testnr), .en(first_wrong), .clk(clk), .Q(WRONG_ADDR));  // open: clr
  Register #(.width(28)) WRONG_X_R (.D(testx), .en(first_wrong), .clk(clk), .Q(WRONG_X));  // open: clr
  Register #(.width(28)) WRONG_Y_R (.D(testy), .en(first_wrong), .clk(clk), .Q(WRONG_Y));  // open: clr
  Counter #(.ongoal("stay")) PASSCNT (.count(dut_pass), .Q(PASSES), .clk(clk));  // open: load, D, carry, up, clr
  Counter #(.ongoal("stay")) FAILCNT (.count(fail), .Q(FAILS), .clk(clk));  // open: load, D, carry, up, clr
  Counter #(.ongoal("stay")) TMOCNT (.count(timeout), .Q(TIMEOUTS), .clk(clk));  // open: load, D, carry, up, clr

  // Other names for the same wires on the sheet: pass = dut_pass; stop = halt

  // Notes on the sheet:
  //   Tohle je tzv. baterie testu, neboli kolekce testu, ktere se spusti postupne po sobe
  //   Obvod se resetuje resetem simulace (Ctrl+R) a pote staci mit zapnuty clock
  //   wrong_stop
  //   contents of Y_ROM (hex, n*v repeats v):
  //   30000 10000 a0000 0 1bb67 50000 80000 70000 140000 c0000 90000 1c0000 b0000 100000 210000 300000
  //   d0000 240000 270000 410000 140000 3c0000 f0000 2c0000 580000 110000 180000 330000 550000 770000
  //   340000 130000 390000 680000 5f0000 1c0000 540000 850000 150000 8c0000 3c0000 690000 780000 200000
  //   170000 600000 450000 730000 a00000 a10000 440000
  //   contents of X_ROM (hex, n*v repeats v):
  //   40000 10000 0 a0000 27311 c0000 f0000 180000 150000 230000 280000 2d0000 3c0000 3f0000 380000 370000
  //   540000 4d0000 500000 480000 630000 5b0000 700000 750000 690000 900000 8f0000 8c0000 840000 780000
  //   a50000 b40000 b00000 990000 a80000 c30000 bb0000 9c0000 dc0000 ab0000 dd0000 d00000 d10000 ff0000
  //   1080000 f70000 1040000 fc0000 e70000 f00000 11d0000
  //   test count
endmodule

module NORM_SINGLE (
  output [27:0] OUTP,
  output halt,
  output done,
  output [27:0] X,
  output [27:0] Y,
  output start
);

  wire clock_1_out;

  S_R_Flip_Flop s_r_ff_1 (.S(start), .R(1'b0), .clk(clock_1_out), .Qn(start));  // open: Q, reset, preset
  Clock clock_1 (.out(clock_1_out));
  NORM norm_1 (
    .X_IN(28'h30000), .Y_IN(28'h40000), .START(start), .CLK(clock_1_out), .OUTP(OUTP), .DONE(done),
    .DEBUG_X(X), .DEBUG_Y(Y));

  assign halt = done;
endmodule
