// Logisim project memory_blank.circ as structural Verilog
module SR_latch (
  input  R,
  input  S,
  output Q,
  output notQ
);
endmodule

module Gated_SR_latch (
  input  R,
  input  S,
  input  E,
  output Q,
  output notQ
);

  wire undriven, undriven_2;

  SR_latch sr_latch_1 (.R(undriven), .S(undriven_2), .Q(Q), .notQ(notQ));
endmodule

module D_latch (
  input  D,
  input  E,
  output Q,
  output notQ
);

  Gated_SR_latch gated_sr_latch_1 (.E(E), .Q(Q), .notQ(notQ));  // open: R, S
endmodule

module RisingEdge (
  input  CLK,
  output PULSE
);

  wire not_1_out, not_2_out, not_3_out;

  not not_1 (not_1_out, CLK);
  not not_2 (not_2_out, not_1_out);
  not not_3 (not_3_out, not_2_out);
  and and_1 (PULSE, not_3_out, CLK);
endmodule

module FallingEdge (
  input  CLK,
  output PULSE
);

  wire not_1_out;

  not not_1 (not_1_out, CLK);
  RisingEdge risingedge_1 (.CLK(not_1_out), .PULSE(PULSE));
endmodule

module D_flipflop_risingedge (
  input  D,
  input  CLK,
  output Q,
  output notQ
);

  wire undriven;

  D_latch d_latch_1 (.D(D), .E(undriven), .Q(Q), .notQ(notQ));
endmodule

module D_flipflop_masterslave (
  input  D,
  input  CLK,
  output Q,
  output notQ
);

  wire d_latch_1_q, undriven, undriven_2;

  D_latch d_latch_1 (.D(D), .E(undriven), .Q(d_latch_1_q));  // open: notQ
  D_latch d_latch_2 (.D(d_latch_1_q), .E(undriven_2), .Q(Q), .notQ(notQ));
endmodule

module Register4 (
  input  [3:0] D,
  input  CLK,
  output [3:0] Q
);

  wire d_flipflop_masterslave_1_q, d_flipflop_masterslave_2_q, d_flipflop_masterslave_3_q,
       d_flipflop_masterslave_4_q, undriven, undriven_2, undriven_3, undriven_4;

  D_flipflop_masterslave d_flipflop_masterslave_1 (
    .D(undriven), .CLK(CLK), .Q(d_flipflop_masterslave_1_q));  // open: notQ
  D_flipflop_masterslave d_flipflop_masterslave_2 (
    .D(undriven_2), .CLK(CLK), .Q(d_flipflop_masterslave_2_q));  // open: notQ
  D_flipflop_masterslave d_flipflop_masterslave_3 (
    .D(undriven_3), .CLK(CLK), .Q(d_flipflop_masterslave_3_q));  // open: notQ
  D_flipflop_masterslave d_flipflop_masterslave_4 (
    .D(undriven_4), .CLK(CLK), .Q(d_flipflop_masterslave_4_q));  // open: notQ
endmodule

module Register16 (
  input  [15:0] D,
  input  CLK,
  output [15:0] Q
);

  wire [3:0] register4_1_q, register4_2_q, register4_3_q, register4_4_q, undriven, undriven_2, undriven_3,
       undriven_4;

  Register4 register4_1 (.D(undriven), .CLK(CLK), .Q(register4_1_q));
  Register4 register4_2 (.D(undriven_2), .CLK(CLK), .Q(register4_2_q));
  Register4 register4_3 (.D(undriven_3), .CLK(CLK), .Q(register4_3_q));
  Register4 register4_4 (.D(undriven_4), .CLK(CLK), .Q(register4_4_q));
endmodule

module Register_WE_Bad (
  input  [15:0] D,
  input  CLK,
  input  WE,
  output [15:0] Q
);

  wire and_1_out;

  and and_1 (and_1_out, CLK, WE);
  Register16 register16_1 (.D(D), .CLK(and_1_out), .Q(Q));

  // Notes on the sheet:
  //   Gated clock is bad!
endmodule

module Register_WE (
  input  [15:0] D,
  input  CLK,
  input  WE,
  output [15:0] Q
);

  Register16 register16_1 (.CLK(CLK), .Q(Q));  // open: D
endmodule

module ShiftRegister (
  input  D_IN,
  input  CLK,
  input  WE,
  output [4:0] PAR_OUT,
  output D_OUT
);

  Register #(.width(1)) register_1 (.D(D_IN), .en(WE), .clk(CLK), .Q(PAR_OUT[0]));  // open: clr
  Register #(.width(1)) register_2 (.D(PAR_OUT[0]), .en(WE), .clk(CLK), .Q(PAR_OUT[1]));  // open: clr
  Register #(.width(1)) register_3 (.D(PAR_OUT[1]), .en(WE), .clk(CLK), .Q(PAR_OUT[2]));  // open: clr
  Register #(.width(1)) register_4 (.D(PAR_OUT[2]), .en(WE), .clk(CLK), .Q(PAR_OUT[3]));  // open: clr
  Register #(.width(1)) register_5 (.D(PAR_OUT[3]), .en(WE), .clk(CLK), .Q(D_OUT));  // open: clr

  assign PAR_OUT[4] = D_OUT;
endmodule

module ShiftRegister8 (
  input  [7:0] D_IN,
  input  CLK,
  input  WE,
  output [39:0] PAR_OUT,
  output [7:0] D_OUT
);

  Register register_1 (.D(D_IN), .en(WE), .clk(CLK), .Q(PAR_OUT[7:0]));  // open: clr
  Register register_2 (.D(PAR_OUT[7:0]), .en(WE), .clk(CLK), .Q(PAR_OUT[15:8]));  // open: clr
  Register register_3 (.D(PAR_OUT[15:8]), .en(WE), .clk(CLK), .Q(PAR_OUT[23:16]));  // open: clr
  Register register_4 (.D(PAR_OUT[23:16]), .en(WE), .clk(CLK), .Q(PAR_OUT[31:24]));  // open: clr
  Register register_5 (.D(PAR_OUT[31:24]), .en(WE), .clk(CLK), .Q(D_OUT));  // open: clr

  assign PAR_OUT[39:32] = D_OUT;
endmodule

module Memory16x4 (
  input  [15:0] D_IN,
  input  CLK,
  input  WE,
  input  [1:0] ADDR,
  output [15:0] D_OUT
);

  wire undriven, undriven_2, undriven_3, undriven_4;
  wire [15:0] register_1_q, register_2_q, register_3_q, register_4_q;

  Register #(.width(16)) register_1 (.D(D_IN), .en(undriven_4), .clk(CLK), .Q(register_1_q));  // open: clr
  Register #(.width(16)) register_2 (.D(D_IN), .en(undriven), .clk(CLK), .Q(register_2_q));  // open: clr
  Register #(.width(16)) register_3 (.D(D_IN), .en(undriven_2), .clk(CLK), .Q(register_3_q));  // open: clr
  Register #(.width(16)) register_4 (.D(D_IN), .en(undriven_3), .clk(CLK), .Q(register_4_q));  // open: clr
endmodule

module Memory16x16 (
  input  [15:0] D_IN,
  input  CLK,
  input  WE,
  input  [3:0] ADDR,
  output [15:0] D_OUT
);

  wire undriven, undriven_2, undriven_3, undriven_4;
  wire [1:0] undriven_5;
  wire [15:0] memory16x4_1_d_out, memory16x4_2_d_out, memory16x4_3_d_out, memory16x4_4_d_out;

  Memory16x4 memory16x4_1 (.D_IN(D_IN), .CLK(CLK), .WE(undriven_4), .ADDR(undriven_5), .D_OUT(memory16x4_1_d_out));
  Memory16x4 memory16x4_2 (.D_IN(D_IN), .CLK(CLK), .WE(undriven), .ADDR(undriven_5), .D_OUT(memory16x4_2_d_out));
  Memory16x4 memory16x4_3 (.D_IN(D_IN), .CLK(CLK), .WE(undriven_2), .ADDR(undriven_5), .D_OUT(memory16x4_3_d_out));
  Memory16x4 memory16x4_4 (.D_IN(D_IN), .CLK(CLK), .WE(undriven_3), .ADDR(undriven_5), .D_OUT(memory16x4_4_d_out));
endmodule

module T_flipflop (
  input  T,
  input  CLK,
  output Q
);

  wire undriven;

  Register #(.width(1)) register_1 (.D(undriven), .en(T), .clk(CLK), .Q(Q));  // open: clr
endmodule

module T_flipflop_osc (
);

  wire button_1_out, clock_1_out, digital_oscilloscope_1_p3, t_ff_1_q;

  Clock clock_1 (.out(clock_1_out));
  T_Flip_Flop t_ff_1 (.T(1'b1), .clk(clock_1_out), .Q(t_ff_1_q), .reset(button_1_out));  // open: Qn, preset
  Button button_1 (.out(button_1_out));
  // Digital_Oscilloscope digital_oscilloscope_1: pin names not known; wires that end beside it: clock_1_out, t_ff_1_q, digital_oscilloscope_1_p3
  Button button_2 (.out(digital_oscilloscope_1_p3));
endmodule

module T_flipflop_osc2 (
);

  wire button_1_out, clock_1_out, digital_oscilloscope_1_p4, digital_oscilloscope_1_p5, t_ff_1_q, t_ff_2_q;

  Clock clock_1 (.out(clock_1_out));
  T_Flip_Flop t_ff_1 (.T(1'b1), .clk(clock_1_out), .Q(t_ff_1_q), .reset(button_1_out));  // open: Qn, preset
  Button button_1 (.out(button_1_out));
  T_Flip_Flop t_ff_2 (.T(1'b1), .clk(t_ff_1_q), .Q(t_ff_2_q), .reset(button_1_out));  // open: Qn, preset
  // Digital_Oscilloscope digital_oscilloscope_1: pin names not known; wires that end beside it: clock_1_out, t_ff_1_q, t_ff_2_q, digital_oscilloscope_1_p4, digital_oscilloscope_1_p5
  T_Flip_Flop t_ff_3 (
    .T(1'b1), .clk(t_ff_2_q), .Q(digital_oscilloscope_1_p4), .reset(button_1_out));  // open: Qn, preset
  Button button_2 (.out(digital_oscilloscope_1_p5));
endmodule

module double_dabble_seq (
  input  [15:0] inp,
  input  start,
  input  work,
  input  clk,
  input  rst,
  output done,
  output [15:0] outp
);

  wire comparator_1_gt, comparator_2_gt, comparator_3_gt, comparator_4_gt, input_zero, next_bit, no_add,
       or_1_out;
  wire [3:0] multiplexer_2_out, multiplexer_3_out, multiplexer_4_out, multiplexer_5_out;
  wire [3:3] adder_4_out;
  wire [15:0] multiplexer_1_out;
  wire [15:1] adder_1_out, input_reg_q;

  Register #(.width(4)) the_1 (.D({adder_1_out[3:1], next_bit}), .en(work), .clk(clk), .Q(outp[3:0]), .clr(rst));
  Register #(.width(4)) the_10 (.D(adder_1_out[7:4]), .en(work), .clk(clk), .Q(outp[7:4]), .clr(rst));
  Register #(.width(4)) the_100 (.D(adder_1_out[11:8]), .en(work), .clk(clk), .Q(outp[11:8]), .clr(rst));
  Register #(.width(4)) the_1000 (.D(adder_1_out[15:12]), .en(work), .clk(clk), .Q(outp[15:12]), .clr(rst));
  or or_1 (or_1_out, start, work);
  Comparator #(.mode("unsigned"), .width(4)) comparator_1 (
    .a(outp[3:0]), .b(4'b0100), .gt(comparator_1_gt));  // open: eq, lt
  Comparator #(.mode("unsigned"), .width(4)) comparator_2 (
    .a(outp[7:4]), .b(4'b0100), .gt(comparator_2_gt));  // open: eq, lt
  Comparator #(.mode("unsigned"), .width(4)) comparator_3 (
    .a(outp[11:8]), .b(4'b0100), .gt(comparator_3_gt));  // open: eq, lt
  Comparator #(.mode("unsigned"), .width(4)) comparator_4 (
    .a(outp[15:12]), .b(4'b0100), .gt(comparator_4_gt));  // open: eq, lt
  Register #(.width(16)) input_reg (
    .D(multiplexer_1_out), .en(or_1_out), .clk(clk), .Q({next_bit, input_reg_q}), .clr(rst));
  Multiplexer #(.width(16)) multiplexer_1 (.in0({input_reg_q, 1'b0}), .in1(inp), .out(multiplexer_1_out), .sel(start));
  Multiplexer #(.width(4)) multiplexer_2 (.in0(4'b0000), .in1(4'b0011), .out(multiplexer_2_out), .sel(comparator_1_gt));
  Multiplexer #(.width(4)) multiplexer_3 (.in0(4'b0000), .in1(4'b0011), .out(multiplexer_3_out), .sel(comparator_2_gt));
  Multiplexer #(.width(4)) multiplexer_4 (.in0(4'b0000), .in1(4'b0011), .out(multiplexer_4_out), .sel(comparator_3_gt));
  Multiplexer #(.width(4)) multiplexer_5 (.in0(4'b0000), .in1(4'b0011), .out(multiplexer_5_out), .sel(comparator_4_gt));
  and and_1 (no_add, ~comparator_1_gt, ~comparator_2_gt, ~comparator_3_gt, ~comparator_4_gt);  // AND_Gate
  Adder #(.width(4)) adder_1 (.a(outp[3:0]), .b(multiplexer_2_out), .out(adder_1_out[4:1]));  // open: cin, cout
  Adder #(.width(4)) adder_2 (.a(outp[7:4]), .b(multiplexer_3_out), .out(adder_1_out[8:5]));  // open: cin, cout
  Adder #(.width(4)) adder_3 (.a(outp[11:8]), .b(multiplexer_4_out), .out(adder_1_out[12:9]));  // open: cin, cout
  Adder #(.width(4)) adder_4 (
    .a(outp[15:12]), .b(multiplexer_5_out), .out({adder_4_out[3], adder_1_out[15:13]}));  // open: cin, cout
  Comparator #(.width(16)) comparator_5 (.a({next_bit, input_reg_q}), .b({16{1'b0}}), .eq(input_zero));  // open: gt, lt
  and and_2 (done, no_add, input_zero);
endmodule
