// Logisim project sekv_compute_expr.circ as structural Verilog
module addsub (
  input  [15:0] A,
  input  [15:0] B,
  input  CIN,
  input  SUB,
  output [15:0] OUTP,
  output COUT
);

  wire adder_1_cout, subtractor_1_bout;
  wire [15:0] adder_1_out, subtractor_1_out;

  Adder #(.width(16)) adder_1 (.a(A), .b(B), .out(adder_1_out), .cin(CIN), .cout(adder_1_cout));
  Subtractor #(.width(16)) subtractor_1 (.a(A), .b(B), .out(subtractor_1_out), .bin(CIN), .bout(subtractor_1_bout));
  Multiplexer #(.width(16)) multiplexer_1 (.in0(adder_1_out), .in1(subtractor_1_out), .out(OUTP), .sel(SUB));
  Multiplexer multiplexer_2 (.in0(adder_1_cout), .in1(subtractor_1_bout), .out(COUT), .sel(SUB));
endmodule

module compute_expr (
  input  [15:0] A,
  input  [15:0] B,
  input  [15:0] C,
  input  [15:0] D,
  input  start,
  input  clk,
  output [15:0] OUTP,
  output done
);

  addsub addsub_1 ();  // open: A, B, CIN, SUB, OUTP, COUT

  // Notes on the sheet:
  //   Expression: (A-B) + (C-D)
endmodule

module compute_expr_0 (
  input  [15:0] A,
  input  [15:0] B,
  input  [15:0] C,
  input  [15:0] D,
  input  start,
  input  clk,
  output [15:0] OUTP,
  output done
);

  wire do_sub, input_we, output_we, tmp1_we, tmp2_we;
  wire [15:0] IN_A_q, IN_B_q, IN_C_q, IN_D_q, register_1_q, register_2_q, undriven, undriven_2, undriven_3;

  Register #(.width(16)) IN_A (.D(A), .en(input_we), .clk(clk), .Q(IN_A_q));  // open: clr
  Register #(.width(16)) IN_B (.D(B), .en(input_we), .clk(clk), .Q(IN_B_q));  // open: clr
  Register #(.width(16)) IN_C (.D(C), .en(input_we), .clk(clk), .Q(IN_C_q));  // open: clr
  Register #(.width(16)) IN_D (.D(D), .en(input_we), .clk(clk), .Q(IN_D_q));  // open: clr
  Register #(.width(16)) register_1 (.D(undriven), .en(tmp1_we), .clk(clk), .Q(register_1_q));  // open: clr
  Register #(.width(16)) register_2 (.D(undriven_2), .en(tmp2_we), .clk(clk), .Q(register_2_q));  // open: clr
  addsub addsub_1 (.CIN(1'b0), .SUB(do_sub));  // open: A, B, OUTP, COUT
  Register #(.width(16)) OUTP_R (.D(undriven_3), .en(output_we), .clk(clk), .Q(OUTP));  // open: clr

  // Notes on the sheet:
  //   inputs
  //   Expression: (A-B) + (C-D)
  //   temporaries
  //   outputs
endmodule

module compute_expr_1 (
  input  [15:0] A,
  input  [15:0] B,
  input  [15:0] C,
  input  [15:0] D,
  input  start,
  input  clk,
  output [15:0] OUTP,
  output done
);

  wire do_sub, input_we, output_we, tmp1_we, tmp2_we;
  wire [1:0] a_src, b_src;
  wire [15:0] addsub_1_outp, IN_A_q, IN_B_q, IN_C_q, IN_D_q, multiplexer_1_out, multiplexer_2_out, T1_q, T2_q;

  Register #(.width(16)) IN_A (.D(A), .en(input_we), .clk(clk), .Q(IN_A_q));  // open: clr
  Register #(.width(16)) IN_B (.D(B), .en(input_we), .clk(clk), .Q(IN_B_q));  // open: clr
  Register #(.width(16)) IN_C (.D(C), .en(input_we), .clk(clk), .Q(IN_C_q));  // open: clr
  Register #(.width(16)) IN_D (.D(D), .en(input_we), .clk(clk), .Q(IN_D_q));  // open: clr
  Multiplexer #(.select(2), .width(16)) multiplexer_1 (
    .in0(IN_A_q), .in1(IN_C_q), .in2(T1_q), .out(multiplexer_1_out), .sel(a_src));  // open: in3
  Multiplexer #(.select(2), .width(16)) multiplexer_2 (
    .in0(IN_B_q), .in1(IN_D_q), .in2(T2_q), .out(multiplexer_2_out), .sel(b_src));  // open: in3
  Register #(.width(16)) T1 (.D(addsub_1_outp), .en(tmp1_we), .clk(clk), .Q(T1_q));  // open: clr
  Register #(.width(16)) T2 (.D(addsub_1_outp), .en(tmp2_we), .clk(clk), .Q(T2_q));  // open: clr
  addsub addsub_1 (
    .A(multiplexer_1_out), .B(multiplexer_2_out), .CIN(1'b0), .SUB(do_sub), .OUTP(addsub_1_outp));  // open: COUT
  Register #(.width(16)) OUTP_R (.D(addsub_1_outp), .en(output_we), .clk(clk), .Q(OUTP));  // open: clr

  // Notes on the sheet:
  //   inputs
  //   Expression: (A-B) + (C-D)
  //   temporaries
  //   outputs
  //   0=A, 1=C, 2=T1
  //   0=B, 1=D, 2=T2
endmodule

module compute_expr_2 (
  input  [15:0] A,
  input  [15:0] B,
  input  [15:0] C,
  input  [15:0] D,
  input  start,
  input  clk,
  output [15:0] OUTP,
  output done
);

  wire do_sub, input_we, output_we, s0, s1, s2, s3, s4, s5, s6, s7, step_we, tmp1_we, tmp2_we;
  wire [1:0] a_src, b_src;
  wire [2:0] adder_1_out, multiplexer_1_out, STEP_q;
  wire [15:0] addsub_1_outp, IN_A_q, IN_B_q, IN_C_q, IN_D_q, multiplexer_2_out, multiplexer_3_out, T1_q, T2_q;

  Register #(.width(16)) IN_A (.D(A), .en(input_we), .clk(clk), .Q(IN_A_q));  // open: clr
  Register #(.width(16)) IN_B (.D(B), .en(input_we), .clk(clk), .Q(IN_B_q));  // open: clr
  Register #(.width(16)) IN_C (.D(C), .en(input_we), .clk(clk), .Q(IN_C_q));  // open: clr
  Register #(.width(16)) IN_D (.D(D), .en(input_we), .clk(clk), .Q(IN_D_q));  // open: clr
  Register #(.width(3)) STEP (.D(multiplexer_1_out), .en(step_we), .clk(clk), .Q(STEP_q));  // open: clr
  Multiplexer #(.width(3)) multiplexer_1 (.in0(adder_1_out), .in1(3'b000), .out(multiplexer_1_out), .sel(start));
  Adder #(.width(3)) adder_1 (.a(3'b001), .b(STEP_q), .out(adder_1_out));  // open: cin, cout
  Decoder #(.enable("false"), .select(3)) decoder_1 (
    .out0(s0), .out1(s1), .out2(s2), .out3(s3), .out4(s4), .out5(s5), .out6(s6), .out7(s7), .sel(STEP_q));
  Multiplexer #(.select(2), .width(16)) multiplexer_2 (
    .in0(IN_A_q), .in1(IN_C_q), .in2(T1_q), .out(multiplexer_2_out), .sel(a_src));  // open: in3
  Multiplexer #(.select(2), .width(16)) multiplexer_3 (
    .in0(IN_B_q), .in1(IN_D_q), .in2(T2_q), .out(multiplexer_3_out), .sel(b_src));  // open: in3
  Register #(.width(16)) T1 (.D(addsub_1_outp), .en(tmp1_we), .clk(clk), .Q(T1_q));  // open: clr
  Register #(.width(16)) T2 (.D(addsub_1_outp), .en(tmp2_we), .clk(clk), .Q(T2_q));  // open: clr
  addsub addsub_1 (
    .A(multiplexer_2_out), .B(multiplexer_3_out), .CIN(1'b0), .SUB(do_sub), .OUTP(addsub_1_outp));  // open: COUT
  Register #(.width(16)) OUTP_R (.D(addsub_1_outp), .en(output_we), .clk(clk), .Q(OUTP));  // open: clr

  // Notes on the sheet:
  //   inputs
  //   Expression: (A-B) + (C-D)
  //   temporaries
  //   outputs
  //   0=A, 1=C, 2=T1
  //   0=B, 1=D, 2=T2
endmodule

module compute_expr_3 (
  input  [15:0] A,
  input  [15:0] B,
  input  [15:0] C,
  input  [15:0] D,
  input  start,
  input  clk,
  output [15:0] OUTP,
  output done
);

  wire do_sub, input_we, output_we, s0, s1, s2, s3, s4, s5, s6, s7, step_we, tmp1_we, tmp2_we;
  wire [1:0] a_src, b_src;
  wire [2:0] adder_1_out, multiplexer_1_out, STEP_q;
  wire [15:0] addsub_1_outp, IN_A_q, IN_B_q, IN_C_q, IN_D_q, multiplexer_2_out, multiplexer_3_out, T1_q, T2_q;

  Register #(.width(16)) IN_A (.D(A), .en(input_we), .clk(clk), .Q(IN_A_q));  // open: clr
  Register #(.width(16)) IN_B (.D(B), .en(input_we), .clk(clk), .Q(IN_B_q));  // open: clr
  Register #(.width(16)) IN_C (.D(C), .en(input_we), .clk(clk), .Q(IN_C_q));  // open: clr
  Register #(.width(16)) IN_D (.D(D), .en(input_we), .clk(clk), .Q(IN_D_q));  // open: clr
  Register #(.width(3)) STEP (.D(multiplexer_1_out), .en(step_we), .clk(clk), .Q(STEP_q));  // open: clr
  Multiplexer #(.width(3)) multiplexer_1 (.in0(adder_1_out), .in1(3'b000), .out(multiplexer_1_out), .sel(start));
  Adder #(.width(3)) adder_1 (.a(3'b001), .b(STEP_q), .out(adder_1_out));  // open: cin, cout
  Decoder #(.enable("false"), .select(3)) decoder_1 (
    .out0(s0), .out1(s1), .out2(s2), .out3(s3), .out4(s4), .out5(s5), .out6(s6), .out7(s7), .sel(STEP_q));
  Multiplexer #(.select(2), .width(16)) multiplexer_2 (
    .in0(IN_A_q), .in1(IN_C_q), .in2(T1_q), .out(multiplexer_2_out), .sel(a_src));  // open: in3
  Multiplexer #(.select(2), .width(16)) multiplexer_3 (
    .in0(IN_B_q), .in1(IN_D_q), .in2(T2_q), .out(multiplexer_3_out), .sel(b_src));  // open: in3
  Register #(.width(16)) T1 (.D(addsub_1_outp), .en(tmp1_we), .clk(clk), .Q(T1_q));  // open: clr
  Register #(.width(16)) T2 (.D(addsub_1_outp), .en(tmp2_we), .clk(clk), .Q(T2_q));  // open: clr
  addsub addsub_1 (
    .A(multiplexer_2_out), .B(multiplexer_3_out), .CIN(1'b0), .SUB(do_sub), .OUTP(addsub_1_outp));  // open: COUT
  Register #(.width(16)) OUTP_R (.D(addsub_1_outp), .en(output_we), .clk(clk), .Q(OUTP));  // open: clr
  // OR_Gate or_1 has open pins: out=do_sub
  buf or_2 (input_we, start);  // OR_Gate
  // OR_Gate or_3 has open pins: out=output_we
  // OR_Gate or_4 has open pins: out=tmp1_we
  // OR_Gate or_5 has open pins: out=tmp2_we
  buf or_6 (step_we, start);  // OR_Gate
  // OR_Gate or_7 has open pins: out=done

  // Notes on the sheet:
  //   inputs
  //   Expression: (A-B) + (C-D)
  //   temporaries
  //   outputs
  //   0=A, 1=C, 2=T1
  //   0=B, 1=D, 2=T2
endmodule

module compute_expr_4 (
  input  [15:0] A,
  input  [15:0] B,
  input  [15:0] C,
  input  [15:0] D,
  input  start,
  input  clk,
  output [15:0] OUTP,
  output done
);

  wire do_sub, input_we, output_we, s0, s1, s2, s3, s4, s5, s6, s7, step_we, tmp1_we, tmp2_we;
  wire [1:0] a_src, b_src;
  wire [2:0] adder_1_out, multiplexer_1_out, step;
  wire [15:0] addsub_1_outp, IN_A_q, IN_B_q, IN_C_q, IN_D_q, multiplexer_2_out, multiplexer_3_out, T1_q, T2_q;

  Register #(.width(16)) IN_A (.D(A), .en(input_we), .clk(clk), .Q(IN_A_q));  // open: clr
  Register #(.width(16)) IN_B (.D(B), .en(input_we), .clk(clk), .Q(IN_B_q));  // open: clr
  Register #(.width(16)) IN_C (.D(C), .en(input_we), .clk(clk), .Q(IN_C_q));  // open: clr
  Register #(.width(16)) IN_D (.D(D), .en(input_we), .clk(clk), .Q(IN_D_q));  // open: clr
  Register #(.width(3)) u_STEP (.D(multiplexer_1_out), .en(step_we), .clk(clk), .Q(step));  // open: clr
  Multiplexer #(.width(3)) multiplexer_1 (.in0(adder_1_out), .in1(3'b000), .out(multiplexer_1_out), .sel(start));
  Adder #(.width(3)) adder_1 (.a(3'b001), .b(step), .out(adder_1_out));  // open: cin, cout
  Decoder #(.enable("false"), .select(3)) decoder_1 (
    .out0(s0), .out1(s1), .out2(s2), .out3(s3), .out4(s4), .out5(s5), .out6(s6), .out7(s7), .sel(step));
  Multiplexer #(.select(2), .width(16)) multiplexer_2 (
    .in0(IN_A_q), .in1(IN_C_q), .in2(T1_q), .out(multiplexer_2_out), .sel(a_src));  // open: in3
  Multiplexer #(.select(2), .width(16)) multiplexer_3 (
    .in0(IN_B_q), .in1(IN_D_q), .in2(T2_q), .out(multiplexer_3_out), .sel(b_src));  // open: in3
  Register #(.width(16)) T1 (.D(addsub_1_outp), .en(tmp1_we), .clk(clk), .Q(T1_q));  // open: clr
  Register #(.width(16)) T2 (.D(addsub_1_outp), .en(tmp2_we), .clk(clk), .Q(T2_q));  // open: clr
  addsub addsub_1 (
    .A(multiplexer_2_out), .B(multiplexer_3_out), .CIN(1'b0), .SUB(do_sub), .OUTP(addsub_1_outp));  // open: COUT
  Register #(.width(16)) OUTP_R (.D(addsub_1_outp), .en(output_we), .clk(clk), .Q(OUTP));  // open: clr
  // OR_Gate or_1 has open pins: out=do_sub
  buf or_2 (input_we, start);  // OR_Gate
  // OR_Gate or_3 has open pins: out=output_we
  // OR_Gate or_4 has open pins: out=tmp1_we
  // OR_Gate or_5 has open pins: out=tmp2_we
  Multiplexer #(.select(3), .width(2)) multiplexer_4 (
    .in0(2'b00), .in1(2'b00), .in2(2'b00), .in3(2'b00), .in4(2'b00), .in5(2'b00), .in6(2'b00), .in7(2'b00),
    .out(a_src), .sel(step));
  Multiplexer #(.select(3), .width(2)) multiplexer_5 (
    .in0(2'b00), .in1(2'b00), .in2(2'b00), .in3(2'b00), .in4(2'b00), .in5(2'b00), .in6(2'b00), .in7(2'b00),
    .out(b_src), .sel(step));
  buf or_6 (step_we, start);  // OR_Gate
  // OR_Gate or_7 has open pins: out=done

  // Notes on the sheet:
  //   inputs
  //   Expression: (A-B) + (C-D)
  //   temporaries
  //   outputs
  //   0=A, 1=C, 2=T1
  //   0=B, 1=D, 2=T2
endmodule

module compute_expr_5 (
  input  [15:0] A,
  input  [15:0] B,
  input  [15:0] C,
  input  [15:0] D,
  input  start,
  input  clk,
  output [15:0] OUTP,
  output done
);

  wire do_sub, input_we, not_1_out, output_we, s0, s1, s2, s3, s4, s5, s6, s7, step_we, tmp1_we, tmp2_we;
  wire [1:0] a_src, b_src;
  wire [2:0] adder_1_out, multiplexer_1_out, step;
  wire [15:0] addsub_1_outp, IN_A_q, IN_B_q, IN_C_q, IN_D_q, multiplexer_2_out, multiplexer_3_out, T1_q, T2_q;

  Register #(.width(16)) IN_A (.D(A), .en(input_we), .clk(clk), .Q(IN_A_q));  // open: clr
  Register #(.width(16)) IN_B (.D(B), .en(input_we), .clk(clk), .Q(IN_B_q));  // open: clr
  Register #(.width(16)) IN_C (.D(C), .en(input_we), .clk(clk), .Q(IN_C_q));  // open: clr
  Register #(.width(16)) IN_D (.D(D), .en(input_we), .clk(clk), .Q(IN_D_q));  // open: clr
  Register #(.width(3)) u_STEP (.D(multiplexer_1_out), .en(step_we), .clk(clk), .Q(step));  // open: clr
  Multiplexer #(.width(3)) multiplexer_1 (.in0(adder_1_out), .in1(3'b000), .out(multiplexer_1_out), .sel(start));
  Adder #(.width(3)) adder_1 (.a(3'b001), .b(step), .out(adder_1_out));  // open: cin, cout
  Decoder #(.enable("false"), .select(3)) decoder_1 (
    .out0(s0), .out1(s1), .out2(s2), .out3(s3), .out4(s4), .out5(s5), .out6(s6), .out7(s7), .sel(step));
  Multiplexer #(.select(2), .width(16)) multiplexer_2 (
    .in0(IN_A_q), .in1(IN_C_q), .in2(T1_q), .out(multiplexer_2_out), .sel(a_src));  // open: in3
  Multiplexer #(.select(2), .width(16)) multiplexer_3 (
    .in0(IN_B_q), .in1(IN_D_q), .in2(T2_q), .out(multiplexer_3_out), .sel(b_src));  // open: in3
  // Probe on multiplexer_2_out
  // Probe on multiplexer_3_out
  Register #(.width(16)) T1 (.D(addsub_1_outp), .en(tmp1_we), .clk(clk), .Q(T1_q));  // open: clr
  Register #(.width(16)) T2 (.D(addsub_1_outp), .en(tmp2_we), .clk(clk), .Q(T2_q));  // open: clr
  // Probe on addsub_1_outp
  addsub addsub_1 (
    .A(multiplexer_2_out), .B(multiplexer_3_out), .CIN(1'b0), .SUB(do_sub), .OUTP(addsub_1_outp));  // open: COUT
  Register #(.width(16)) OUTP_R (.D(addsub_1_outp), .en(output_we), .clk(clk), .Q(OUTP));  // open: clr
  not not_1 (not_1_out, s3);
  or or_1 (do_sub, s0, s1);
  buf or_2 (input_we, start);  // OR_Gate
  buf or_3 (output_we, s2);  // OR_Gate
  buf or_4 (tmp1_we, s0);  // OR_Gate
  buf or_5 (tmp2_we, s1);  // OR_Gate
  Multiplexer #(.select(3), .width(2)) multiplexer_4 (
    .in0(2'b00), .in1(2'b01), .in2(2'b10), .in3(2'b00), .in4(2'b00), .in5(2'b00), .in6(2'b00), .in7(2'b00),
    .out(a_src), .sel(step));
  Multiplexer #(.select(3), .width(2)) multiplexer_5 (
    .in0(2'b00), .in1(2'b01), .in2(2'b10), .in3(2'b00), .in4(2'b00), .in5(2'b00), .in6(2'b00), .in7(2'b00),
    .out(b_src), .sel(step));
  or or_6 (step_we, start, not_1_out);
  buf or_7 (done, s3);  // OR_Gate
  // Probe on a_src
  // Probe on b_src

  // Notes on the sheet:
  //   inputs
  //   Expression: (A-B) + (C-D)
  //   temporaries
  //   outputs
  //   0=A, 1=C, 2=T1
  //   0=B, 1=D, 2=T2
endmodule
