// Logisim project sekv_double_dabble.circ as structural Verilog: 2 circuits, main circuit main
module main (
  input  [15:0] INP,
  input  start,
  input  work,
  input  rst
);

  wire clock_1_out, double_dabble_1_done;
  wire [15:0] double_dabble_1_outp;

  Clock clock_1 (.out(clock_1_out));
  double_dabble double_dabble_1 (
    .inp(INP), .start(start), .work(work), .clk(clock_1_out), .rst(rst), .done(double_dabble_1_done),
    .outp(double_dabble_1_outp));
  _7_Segment_Display u_7_segment_display_1 ();  // open: g, f, a, b, e, d, c, dp
  // BCD_to_7_Segment_decoder bcd_to_7_segment_decoder_1: pin names not known; wires that end beside it: double_dabble_1_outp[15:12]
  LED led_1 (.in(double_dabble_1_done));
  _7_Segment_Display u_7_segment_display_2 ();  // open: g, f, a, b, e, d, c, dp
  // BCD_to_7_Segment_decoder bcd_to_7_segment_decoder_2: pin names not known; wires that end beside it: double_dabble_1_outp[11:8]
  _7_Segment_Display u_7_segment_display_3 ();  // open: g, f, a, b, e, d, c, dp
  _7_Segment_Display u_7_segment_display_4 ();  // open: g, f, a, b, e, d, c, dp
  // BCD_to_7_Segment_decoder bcd_to_7_segment_decoder_3: pin names not known; wires that end beside it: double_dabble_1_outp[7:4]
  // BCD_to_7_Segment_decoder bcd_to_7_segment_decoder_4: pin names not known; wires that end beside it: double_dabble_1_outp[3:0]
endmodule

module double_dabble (
  input  [15:0] inp,
  input  start,
  input  work,
  input  clk,
  input  rst,
  output done,
  output [15:0] outp
);

  wire comparator_1_gt, comparator_2_gt, comparator_3_gt, comparator_4_gt, input_zero, next_bit, or_1_out,
       or_2_out;
  wire [3:0] adder_2_out_2, adder_3_out, adder_4_out, multiplexer_3_out, multiplexer_4_out,
       multiplexer_5_out, multiplexer_6_out;
  wire [3:1] adder_2_out;
  wire [3:3] adder_5_out;
  wire [4:0] adder_1_out, multiplexer_1_out, register_1_q;
  wire [15:0] multiplexer_2_out;
  wire [15:1] input_reg_q;

  // Probe on {adder_2_out, next_bit}
  // Probe on {adder_2_out, next_bit}
  // Probe on adder_2_out_2
  // Probe on adder_2_out_2
  // Probe on adder_3_out
  // Probe on adder_3_out
  // Probe on adder_4_out
  // Probe on adder_4_out
  Adder #(.width(5)) adder_1 (.a(register_1_q), .b(5'b00001), .out(adder_1_out));  // open: cin, cout
  Multiplexer #(.width(5)) multiplexer_1 (.in0(adder_1_out), .in1({5{1'b0}}), .out(multiplexer_1_out), .sel(start));
  or or_1 (or_1_out, start, work);
  Register #(.width(4)) the_1 (.D({adder_2_out, next_bit}), .en(work), .clk(clk), .Q(outp[3:0]), .clr(rst));
  Register #(.width(4)) the_10 (.D(adder_2_out_2), .en(work), .clk(clk), .Q(outp[7:4]), .clr(rst));
  Register #(.width(4)) the_100 (.D(adder_3_out), .en(work), .clk(clk), .Q(outp[11:8]), .clr(rst));
  Register #(.width(4)) the_1000 (.D(adder_4_out), .en(work), .clk(clk), .Q(outp[15:12]), .clr(rst));
  Multiplexer #(.width(16)) multiplexer_2 (.in0({input_reg_q, 1'b0}), .in1(inp), .out(multiplexer_2_out), .sel(start));
  or or_2 (or_2_out, start, work);
  Register #(.width(5)) register_1 (.D(multiplexer_1_out), .en(or_1_out), .clk(clk), .Q(register_1_q), .clr(rst));
  Register #(.width(16)) input_reg (
    .D(multiplexer_2_out), .en(or_2_out), .clk(clk), .Q({next_bit, input_reg_q}), .clr(rst));
  // Probe on outp[3:0]
  Comparator #(.mode("unsigned"), .width(4)) comparator_1 (
    .a(outp[3:0]), .b(4'b0100), .gt(comparator_1_gt));  // open: eq, lt
  // Probe on outp[7:4]
  Comparator #(.mode("unsigned"), .width(4)) comparator_2 (
    .a(outp[7:4]), .b(4'b0100), .gt(comparator_2_gt));  // open: eq, lt
  // Probe on outp[11:8]
  Comparator #(.mode("unsigned"), .width(4)) comparator_3 (
    .a(outp[11:8]), .b(4'b0100), .gt(comparator_3_gt));  // open: eq, lt
  // Probe on outp[15:12]
  Comparator #(.mode("unsigned"), .width(4)) comparator_4 (
    .a(outp[15:12]), .b(4'b0100), .gt(comparator_4_gt));  // open: eq, lt
  // Probe on {next_bit, input_reg_q}
  Comparator #(.width(5)) comparator_5 (.a(register_1_q), .b(5'b10000), .eq(done));  // open: gt, lt
  // Probe on register_1_q
  // Probe on outp[3:0]
  Multiplexer #(.width(4)) multiplexer_3 (.in0(4'b0000), .in1(4'b0011), .out(multiplexer_3_out), .sel(comparator_1_gt));
  // Probe on outp[7:4]
  Multiplexer #(.width(4)) multiplexer_4 (.in0(4'b0000), .in1(4'b0011), .out(multiplexer_4_out), .sel(comparator_2_gt));
  // Probe on outp[11:8]
  Multiplexer #(.width(4)) multiplexer_5 (.in0(4'b0000), .in1(4'b0011), .out(multiplexer_5_out), .sel(comparator_3_gt));
  // Probe on outp[15:12]
  Multiplexer #(.width(4)) multiplexer_6 (.in0(4'b0000), .in1(4'b0011), .out(multiplexer_6_out), .sel(comparator_4_gt));
  Adder #(.width(4)) adder_2 (
    .a(outp[3:0]), .b(multiplexer_3_out), .out({adder_2_out_2[0], adder_2_out}));  // open: cin, cout
  Adder #(.width(4)) adder_3 (
    .a(outp[7:4]), .b(multiplexer_4_out), .out({adder_3_out[0], adder_2_out_2[3:1]}));  // open: cin, cout
  Adder #(.width(4)) adder_4 (
    .a(outp[11:8]), .b(multiplexer_5_out), .out({adder_4_out[0], adder_3_out[3:1]}));  // open: cin, cout
  Adder #(.width(4)) adder_5 (
    .a(outp[15:12]), .b(multiplexer_6_out), .out({adder_5_out[3], adder_4_out[3:1]}));  // open: cin, cout
  Comparator #(.width(16)) comparator_6 (.a({next_bit, input_reg_q}), .b({16{1'b0}}), .eq(input_zero));  // open: gt, lt
  // Probe on {adder_2_out_2[0], adder_2_out}
  // Probe on {adder_2_out_2[0], adder_2_out}
  // Probe on {adder_3_out[0], adder_2_out_2[3:1]}
  // Probe on {adder_3_out[0], adder_2_out_2[3:1]}
  // Probe on {adder_4_out[0], adder_3_out[3:1]}
  // Probe on {adder_4_out[0], adder_3_out[3:1]}
  // Probe on {adder_5_out[3], adder_4_out[3:1]}
  // Probe on {adder_5_out[3], adder_4_out[3:1]}
endmodule
