// Logisim project sekv_exp_sq_mul.circ as structural Verilog
module sq_mul_twomul (
  input  [3:0] A,
  input  [2:0] B,
  input  CLK,
  input  START,
  output [31:0] OUTP,
  output DONE
);

  wire shift_register_1_p3, shift_register_1_p9, we;
  wire [4:0] adder_1_out, multiplexer_1_out, register_1_q;
  wire [31:0] bit_extender_1_out, multiplexer_2_out, multiplexer_3_out, multiplier_1_out, multiplier_2_out;

  Multiplexer #(.width(5)) multiplexer_1 (.in0(adder_1_out), .in1({5{1'b0}}), .out(multiplexer_1_out), .sel(START));
  Register #(.width(5)) register_1 (.D(multiplexer_1_out), .en(we), .clk(CLK), .Q(register_1_q), .clr(1'b0));
  Multiplexer #(.width(32)) multiplexer_2 (.in0(multiplexer_3_out), .in1(32'h1), .out(multiplexer_2_out), .sel(START));
  Register #(.width(32)) ACC (.D(multiplexer_2_out), .en(we), .clk(CLK), .Q(OUTP), .clr(1'b0));
  Adder #(.width(5)) adder_1 (.a(5'b00001), .b(register_1_q), .out(adder_1_out));  // open: cin, cout
  Comparator #(.width(5)) comparator_1 (.a(register_1_q), .b(5'b00011), .eq(DONE));  // open: gt, lt
  Multiplier #(.width(32)) multiplier_1 (.a(OUTP), .b(OUTP), .out(multiplier_1_out));  // open: cin, cout
  or or_1 (we, START, ~DONE);  // OR_Gate
  assign bit_extender_1_out = {{28{1'b0}}, A};  // Bit_Extender bit_extender_1
  // Shift_Register #(.length(3)) shift_register_1: pin names not known; wires that end beside it: 1'b0, START, shift_register_1_p3, CLK, 1'b0, B[0], B[1], B[2], shift_register_1_p9
  not not_1 (shift_register_1_p3, START);
  Multiplier #(.width(32)) multiplier_2 (
    .a(multiplier_1_out), .b(bit_extender_1_out), .out(multiplier_2_out));  // open: cin, cout
  Multiplexer #(.width(32)) multiplexer_3 (
    .in0(multiplier_1_out), .in1(multiplier_2_out), .out(multiplexer_3_out), .sel(shift_register_1_p9));
endmodule

module sq_mul_onemul (
  input  [3:0] A,
  input  [2:0] B,
  input  CLK,
  input  START,
  output [31:0] OUTP,
  output DONE
);

  wire mul, or_2_out, shift_register_1_p3, shift_register_1_p9, we;
  wire [4:0] adder_1_out, multiplexer_1_out, register_1_q;
  wire [31:0] bit_extender_1_out, multiplexer_2_out, multiplexer_3_out, multiplexer_4_out, multiplier_1_out;

  Multiplexer #(.width(5)) multiplexer_1 (.in0(adder_1_out), .in1({5{1'b0}}), .out(multiplexer_1_out), .sel(START));
  Register #(.width(5)) register_1 (.D(multiplexer_1_out), .en(we), .clk(CLK), .Q(register_1_q), .clr(1'b0));
  Multiplexer #(.width(32)) multiplexer_2 (.in0(multiplexer_4_out), .in1(32'h1), .out(multiplexer_2_out), .sel(START));
  Register #(.width(32)) ACC (.D(multiplexer_2_out), .en(we), .clk(CLK), .Q(OUTP), .clr(1'b0));
  Adder #(.width(5)) adder_1 (.a(5'b00001), .b(register_1_q), .out(adder_1_out));  // open: cin, cout
  or or_1 (we, START, ~DONE);  // OR_Gate
  Comparator #(.width(5)) comparator_1 (.a(register_1_q), .b(5'b00101), .eq(DONE));  // open: gt, lt
  not not_1 (mul, register_1_q[0]);
  assign bit_extender_1_out = {{28{1'b0}}, A};  // Bit_Extender bit_extender_1
  Multiplexer #(.width(32)) multiplexer_3 (.in0(OUTP), .in1(bit_extender_1_out), .out(multiplexer_3_out), .sel(mul));
  // Shift_Register #(.length(3)) shift_register_1: pin names not known; wires that end beside it: 1'b0, START, shift_register_1_p3, CLK, 1'b0, B[0], B[1], B[2], shift_register_1_p9
  and and_1 (shift_register_1_p3, ~START, mul);  // AND_Gate
  or or_2 (or_2_out, ~mul, shift_register_1_p9);  // OR_Gate
  Multiplier #(.width(32)) multiplier_1 (.a(OUTP), .b(multiplexer_3_out), .out(multiplier_1_out));  // open: cin, cout
  // Probe on multiplexer_4_out
  Multiplexer #(.width(32)) multiplexer_4 (.in0(OUTP), .in1(multiplier_1_out), .out(multiplexer_4_out), .sel(or_2_out));

  // Notes on the sheet:
  //   more cycles
  //   multiply on even cycles
  //   datapath
  //   shift only when mul
  //   if square, force multiplier
endmodule

module mul_double_add_32 (
  input  [31:0] A,
  input  [31:0] B,
  input  CLK,
  input  START,
  output [63:0] OUTP,
  output DONE
);

  wire shift_register_1_p3, undriven, we;
  wire [5:0] adder_1_out, multiplexer_1_out, register_1_q;
  wire [63:0] adder_2_out, bit_extender_1_out, multiplexer_2_out, multiplexer_3_out, shifter_1_out;

  Multiplexer #(.width(6)) multiplexer_1 (.in0(adder_1_out), .in1({6{1'b0}}), .out(multiplexer_1_out), .sel(START));
  Register #(.width(6)) register_1 (.D(multiplexer_1_out), .en(we), .clk(CLK), .Q(register_1_q), .clr(1'b0));
  Multiplexer #(.width(64)) multiplexer_2 (
    .in0(multiplexer_3_out), .in1({64{1'b0}}), .out(multiplexer_2_out), .sel(START));
  Register #(.width(64)) ACC (.D(multiplexer_2_out), .en(we), .clk(CLK), .Q(OUTP), .clr(1'b0));
  Adder #(.width(6)) adder_1 (.a(6'b000001), .b(register_1_q), .out(adder_1_out));  // open: cin, cout
  Comparator #(.width(6)) comparator_1 (.a(register_1_q), .b(6'b100000), .eq(DONE));  // open: gt, lt
  Shifter #(.width(64)) shifter_1 (.in(OUTP), .\dist (6'b000001), .out(shifter_1_out));
  or or_1 (we, START, ~DONE);  // OR_Gate
  // Shift_Register #(.length(32)) shift_register_1: pin names not known; wires that end beside it: 1'b0, START, shift_register_1_p3, CLK, 1'b0
  not not_1 (shift_register_1_p3, START);
  Adder #(.width(64)) adder_2 (.a(shifter_1_out), .b(bit_extender_1_out), .out(adder_2_out));  // open: cin, cout
  assign bit_extender_1_out = {{32{1'b0}}, A};  // Bit_Extender bit_extender_1
  // Probe on multiplexer_3_out
  Multiplexer #(.width(64)) multiplexer_3 (
    .in0(shifter_1_out), .in1(adder_2_out), .out(multiplexer_3_out), .sel(undriven));
endmodule

module sq_mul_sekvmul_0 (
  input  [3:0] A,
  input  [2:0] B,
  input  CLK,
  input  START,
  output [31:0] OUTP,
  output DONE
);

  wire and_1_out, and_2_out, mul, or_2_out, shift_register_1_p9, we;
  wire [4:0] adder_1_out, multiplexer_1_out, register_1_q;
  wire [31:0] bit_extender_1_out, multiplexer_2_out, multiplexer_3_out, multiplexer_4_out, multiplier_1_out;

  Multiplexer #(.width(5)) multiplexer_1 (.in0(adder_1_out), .in1({5{1'b0}}), .out(multiplexer_1_out), .sel(START));
  Register #(.width(5)) register_1 (.D(multiplexer_1_out), .en(we), .clk(CLK), .Q(register_1_q), .clr(1'b0));
  Multiplexer #(.width(32)) multiplexer_2 (.in0(multiplexer_4_out), .in1(32'h1), .out(multiplexer_2_out), .sel(START));
  Register #(.width(32)) ACC (.D(multiplexer_2_out), .en(we), .clk(CLK), .Q(OUTP), .clr(1'b0));
  Adder #(.width(5)) adder_1 (.a(5'b00001), .b(register_1_q), .out(adder_1_out));  // open: cin, cout
  Comparator #(.width(5)) comparator_1 (.a(register_1_q), .b(5'b00101), .eq(DONE));  // open: gt, lt
  not not_1 (mul, register_1_q[0]);
  assign bit_extender_1_out = {{28{1'b0}}, A};  // Bit_Extender bit_extender_1
  Multiplexer #(.width(32)) multiplexer_3 (.in0(OUTP), .in1(bit_extender_1_out), .out(multiplexer_3_out), .sel(mul));
  or or_1 (we, START, ~DONE);  // OR_Gate
  Multiplier #(.width(32)) multiplier_1 (.a(OUTP), .b(multiplexer_3_out), .out(multiplier_1_out));  // open: cin, cout
  and and_1 (and_1_out, ~START, and_2_out);  // AND_Gate
  and and_2 (and_2_out, mul, we);
  // Shift_Register #(.length(3)) shift_register_1: pin names not known; wires that end beside it: 1'b0, START, and_1_out, CLK, 1'b0, B[0], B[1], B[2], shift_register_1_p9
  // Probe on multiplexer_4_out
  Multiplexer #(.width(32)) multiplexer_4 (.in0(OUTP), .in1(multiplier_1_out), .out(multiplexer_4_out), .sel(or_2_out));
  or or_2 (or_2_out, ~mul, shift_register_1_p9);  // OR_Gate

  // Notes on the sheet:
  //   only shift if we and mul
endmodule

module sq_mul_sekvmul_1 (
  input  [3:0] A,
  input  [2:0] B,
  input  CLK,
  input  START,
  output [31:0] OUTP,
  output DONE
);

  wire and_1_out, and_2_out, mul, mult_done, mult_start, or_2_out, shift_register_1_p1, shift_register_1_p10,
       we;
  wire [4:0] adder_1_out, ITER_q, multiplexer_1_out;
  wire [31:0] bit_extender_1_out, bit_extender_2_out, multiplexer_2_out, multiplexer_3_out, multiplexer_4_out;
  wire [63:0] mul_double_add_32_1_outp;

  Multiplexer #(.width(5)) multiplexer_1 (.in0(adder_1_out), .in1({5{1'b0}}), .out(multiplexer_1_out), .sel(START));
  Register #(.width(5)) ITER (.D(multiplexer_1_out), .en(we), .clk(CLK), .Q(ITER_q), .clr(1'b0));
  Multiplexer #(.width(32)) multiplexer_2 (.in0(multiplexer_4_out), .in1(32'h1), .out(multiplexer_2_out), .sel(START));
  Register #(.width(32)) ACC (.D(multiplexer_2_out), .en(we), .clk(CLK), .Q(OUTP), .clr(1'b0));
  Adder #(.width(5)) adder_1 (.a(5'b00001), .b(ITER_q), .out(adder_1_out));  // open: cin, cout
  Comparator #(.width(5)) comparator_1 (.a(ITER_q), .b(5'b00101), .eq(DONE));  // open: gt, lt
  not not_1 (mul, ITER_q[0]);
  assign bit_extender_1_out = {{28{1'b0}}, A};  // Bit_Extender bit_extender_1
  Multiplexer #(.width(32)) multiplexer_3 (.in0(OUTP), .in1(bit_extender_1_out), .out(multiplexer_3_out), .sel(mul));
  or or_1 (we, START, ~DONE);  // OR_Gate
  mul_double_add_32 mul_double_add_32_1 (
    .A(OUTP), .B(multiplexer_3_out), .CLK(shift_register_1_p1), .START(mult_start),
    .OUTP(mul_double_add_32_1_outp), .DONE(mult_done));
  and and_1 (and_1_out, ~START, and_2_out);  // AND_Gate
  and and_2 (and_2_out, mul, we);
  Bit_Extender #(.in_width(64), .out_width(32), .\type ("zero")) bit_extender_2 (
    .in(mul_double_add_32_1_outp), .out(bit_extender_2_out));
  // Shift_Register #(.length(3)) shift_register_1: pin names not known; wires that end beside it: shift_register_1_p1, 1'b0, START, and_1_out, CLK, 1'b0, B[0], B[1], B[2], shift_register_1_p10
  // Probe on multiplexer_4_out
  Multiplexer #(.width(32)) multiplexer_4 (
    .in0(OUTP), .in1(bit_extender_2_out), .out(multiplexer_4_out), .sel(or_2_out));
  or or_2 (or_2_out, ~mul, shift_register_1_p10);  // OR_Gate
endmodule

module sq_mul_sekvmul_2 (
  input  [3:0] A,
  input  [2:0] B,
  input  CLK,
  input  START,
  output [31:0] OUTP,
  output DONE
);

  wire adder_2_out, and_1_out, and_2_out, mul, mult_done, mult_start, multiplexer_2_out, or_2_out,
       shift_register_1_p9, step1, STEP_q, step_we, we;
  wire [4:0] adder_1_out, ITER_q, multiplexer_1_out;
  wire [31:0] bit_extender_1_out, bit_extender_2_out, multiplexer_3_out, multiplexer_4_out, multiplexer_5_out;
  wire [63:0] mul_double_add_32_1_outp;

  Multiplexer #(.width(5)) multiplexer_1 (.in0(adder_1_out), .in1({5{1'b0}}), .out(multiplexer_1_out), .sel(START));
  Multiplexer multiplexer_2 (.in0(adder_2_out), .in1(1'b0), .out(multiplexer_2_out), .sel(START));
  Register #(.width(5)) ITER (.D(multiplexer_1_out), .en(we), .clk(CLK), .Q(ITER_q), .clr(1'b0));
  Register #(.width(1)) STEP (.D(multiplexer_2_out), .en(step_we), .clk(CLK), .Q(STEP_q), .clr(1'b0));
  Multiplexer #(.width(32)) multiplexer_3 (.in0(multiplexer_5_out), .in1(32'h1), .out(multiplexer_3_out), .sel(START));
  Register #(.width(32)) ACC (.D(multiplexer_3_out), .en(we), .clk(CLK), .Q(OUTP), .clr(1'b0));
  Adder #(.width(5)) adder_1 (.a(5'b00001), .b(ITER_q), .out(adder_1_out));  // open: cin, cout
  Adder #(.width(1)) adder_2 (.a(1'b1), .b(STEP_q), .out(adder_2_out));  // open: cin, cout
  Comparator #(.width(5)) comparator_1 (.a(ITER_q), .b(5'b00101), .eq(DONE));  // open: gt, lt
  not not_1 (mul, ITER_q[0]);
  Decoder #(.enable("false")) decoder_1 (.out0(mult_start), .out1(step1), .sel(STEP_q));
  assign bit_extender_1_out = {{28{1'b0}}, A};  // Bit_Extender bit_extender_1
  Multiplexer #(.width(32)) multiplexer_4 (.in0(OUTP), .in1(bit_extender_1_out), .out(multiplexer_4_out), .sel(mul));
  mul_double_add_32 mul_double_add_32_1 (
    .A(OUTP), .B(multiplexer_4_out), .CLK(CLK), .START(mult_start), .OUTP(mul_double_add_32_1_outp),
    .DONE(mult_done));
  and and_1 (and_1_out, ~START, and_2_out);  // AND_Gate
  and and_2 (and_2_out, mul, we);
  or or_1 (we, START, ~DONE);  // OR_Gate
  Bit_Extender #(.in_width(64), .out_width(32), .\type ("zero")) bit_extender_2 (
    .in(mul_double_add_32_1_outp), .out(bit_extender_2_out));
  // Shift_Register #(.length(3)) shift_register_1: pin names not known; wires that end beside it: 1'b0, START, and_1_out, CLK, 1'b0, B[0], B[1], B[2], shift_register_1_p9
  // Probe on multiplexer_5_out
  Multiplexer #(.width(32)) multiplexer_5 (
    .in0(OUTP), .in1(bit_extender_2_out), .out(multiplexer_5_out), .sel(or_2_out));
  or or_2 (or_2_out, ~mul, shift_register_1_p9);  // OR_Gate

  // Other names for the same wires on the sheet: step0 = mult_start

  // Notes on the sheet:
  //   on step0, start multiplication
endmodule

module sq_mul_sekvmul_3 (
  input  [3:0] A,
  input  [2:0] B,
  input  CLK,
  input  START,
  output [31:0] OUTP,
  output DONE
);

  wire adder_2_out, and_1_out, and_2_out, and_3_out, mul, mult_done, mult_start, multiplexer_2_out, or_2_out,
       shift_register_1_p9, step1, STEP_q, step_we, we;
  wire [4:0] adder_1_out, ITER_q, multiplexer_1_out;
  wire [31:0] bit_extender_1_out, bit_extender_2_out, multiplexer_3_out, multiplexer_4_out, multiplexer_5_out;
  wire [63:0] mul_double_add_32_1_outp;

  Multiplexer #(.width(5)) multiplexer_1 (.in0(adder_1_out), .in1({5{1'b0}}), .out(multiplexer_1_out), .sel(START));
  Multiplexer multiplexer_2 (.in0(adder_2_out), .in1(1'b0), .out(multiplexer_2_out), .sel(START));
  Register #(.width(5)) ITER (.D(multiplexer_1_out), .en(we), .clk(CLK), .Q(ITER_q), .clr(1'b0));
  Register #(.width(1)) STEP (.D(multiplexer_2_out), .en(step_we), .clk(CLK), .Q(STEP_q), .clr(1'b0));
  Multiplexer #(.width(32)) multiplexer_3 (.in0(multiplexer_5_out), .in1(32'h1), .out(multiplexer_3_out), .sel(START));
  Register #(.width(32)) ACC (.D(multiplexer_3_out), .en(we), .clk(CLK), .Q(OUTP), .clr(1'b0));
  Adder #(.width(5)) adder_1 (.a(5'b00001), .b(ITER_q), .out(adder_1_out));  // open: cin, cout
  Adder #(.width(1)) adder_2 (.a(1'b1), .b(STEP_q), .out(adder_2_out));  // open: cin, cout
  Comparator #(.width(5)) comparator_1 (.a(ITER_q), .b(5'b00101), .eq(DONE));  // open: gt, lt
  not not_1 (mul, ITER_q[0]);
  Decoder #(.enable("false")) decoder_1 (.out0(mult_start), .out1(step1), .sel(STEP_q));
  assign bit_extender_1_out = {{28{1'b0}}, A};  // Bit_Extender bit_extender_1
  Multiplexer #(.width(32)) multiplexer_4 (.in0(OUTP), .in1(bit_extender_1_out), .out(multiplexer_4_out), .sel(mul));
  and and_1 (and_1_out, ~DONE, step1, mult_done);  // AND_Gate
  mul_double_add_32 mul_double_add_32_1 (
    .A(OUTP), .B(multiplexer_4_out), .CLK(CLK), .START(mult_start), .OUTP(mul_double_add_32_1_outp),
    .DONE(mult_done));
  and and_2 (and_2_out, ~START, and_3_out);  // AND_Gate
  and and_3 (and_3_out, mul, we);
  or or_1 (we, START, and_1_out);
  Bit_Extender #(.in_width(64), .out_width(32), .\type ("zero")) bit_extender_2 (
    .in(mul_double_add_32_1_outp), .out(bit_extender_2_out));
  // Shift_Register #(.length(3)) shift_register_1: pin names not known; wires that end beside it: 1'b0, START, and_2_out, CLK, 1'b0, B[0], B[1], B[2], shift_register_1_p9
  // Probe on multiplexer_5_out
  Multiplexer #(.width(32)) multiplexer_5 (
    .in0(OUTP), .in1(bit_extender_2_out), .out(multiplexer_5_out), .sel(or_2_out));
  or or_2 (or_2_out, ~mul, shift_register_1_p9);  // OR_Gate

  // Other names for the same wires on the sheet: step0 = mult_start

  // Notes on the sheet:
  //   on step0, start multiplication
  //   only we if:
  //   - not done
  //   - on step1
  //   - mult is done
endmodule

module sq_mul_sekvmul_4 (
  input  [3:0] A,
  input  UNTIL_MULT_DONE,
  input  [2:0] B,
  input  CLK,
  input  START,
  output [31:0] OUTP,
  output DONE
);

  wire adder_2_out, and_1_out, and_4_out, and_5_out, and_6_out, and_7_out, clk_t, mul, mult_done, mult_start,
       multiplexer_2_out, or_1_out, or_4_out, shift_register_1_p9, step1, step1_done, STEP_q, step_we, we;
  wire [4:0] adder_1_out, ITER_q, multiplexer_1_out;
  wire [31:0] bit_extender_1_out, bit_extender_2_out, multiplexer_3_out, multiplexer_4_out, multiplexer_5_out;
  wire [63:0] mul_double_add_32_1_outp;

  and and_1 (and_1_out, UNTIL_MULT_DONE, mult_done);
  and and_2 (clk_t, ~and_1_out, CLK);  // AND_Gate
  Multiplexer #(.width(5)) multiplexer_1 (.in0(adder_1_out), .in1({5{1'b0}}), .out(multiplexer_1_out), .sel(START));
  Multiplexer multiplexer_2 (.in0(adder_2_out), .in1(1'b0), .out(multiplexer_2_out), .sel(START));
  Register #(.width(5)) ITER (.D(multiplexer_1_out), .en(we), .clk(clk_t), .Q(ITER_q), .clr(1'b0));
  Register #(.width(1)) STEP (.D(multiplexer_2_out), .en(step_we), .clk(clk_t), .Q(STEP_q), .clr(1'b0));
  Multiplexer #(.width(32)) multiplexer_3 (.in0(multiplexer_5_out), .in1(32'h1), .out(multiplexer_3_out), .sel(START));
  Register #(.width(32)) ACC (.D(multiplexer_3_out), .en(we), .clk(clk_t), .Q(OUTP), .clr(1'b0));
  Adder #(.width(5)) adder_1 (.a(5'b00001), .b(ITER_q), .out(adder_1_out));  // open: cin, cout
  Adder #(.width(1)) adder_2 (.a(1'b1), .b(STEP_q), .out(adder_2_out));  // open: cin, cout
  Comparator #(.width(5)) comparator_1 (.a(ITER_q), .b(5'b00101), .eq(DONE));  // open: gt, lt
  not not_1 (mul, ITER_q[0]);
  Decoder #(.enable("false")) decoder_1 (.out0(mult_start), .out1(step1), .sel(STEP_q));
  and and_3 (step1_done, step1, mult_done);
  assign bit_extender_1_out = {{28{1'b0}}, A};  // Bit_Extender bit_extender_1
  Multiplexer #(.width(32)) multiplexer_4 (.in0(OUTP), .in1(bit_extender_1_out), .out(multiplexer_4_out), .sel(mul));
  and and_4 (and_4_out, ~DONE, step1_done);  // AND_Gate
  or or_1 (or_1_out, mult_start, step1_done);
  mul_double_add_32 mul_double_add_32_1 (
    .A(OUTP), .B(multiplexer_4_out), .CLK(clk_t), .START(mult_start), .OUTP(mul_double_add_32_1_outp),
    .DONE(mult_done));
  and and_5 (and_5_out, ~START, and_6_out);  // AND_Gate
  and and_6 (and_6_out, mul, we);
  or or_2 (we, START, and_4_out);
  or or_3 (step_we, START, and_7_out);
  and and_7 (and_7_out, ~DONE, or_1_out);  // AND_Gate
  Bit_Extender #(.in_width(64), .out_width(32), .\type ("zero")) bit_extender_2 (
    .in(mul_double_add_32_1_outp), .out(bit_extender_2_out));
  // Shift_Register #(.length(3)) shift_register_1: pin names not known; wires that end beside it: 1'b0, START, and_5_out, clk_t, 1'b0, B[0], B[1], B[2], shift_register_1_p9
  // Probe on multiplexer_5_out
  Multiplexer #(.width(32)) multiplexer_5 (
    .in0(OUTP), .in1(bit_extender_2_out), .out(multiplexer_5_out), .sel(or_4_out));
  or or_4 (or_4_out, ~mul, shift_register_1_p9);  // OR_Gate

  // Other names for the same wires on the sheet: step0 = mult_start

  // Notes on the sheet:
  //   only we if:
  //   decision chain for step_we
  //   - not done
  //   - step1 is done
endmodule

module sq_mul_sekvmul_5 (
  input  [3:0] A,
  input  UNTIL_MULT_DONE,
  input  [2:0] B,
  input  CLK,
  input  START,
  output [31:0] OUTP,
  output DONE
);

  wire adder_2_out, and_1_out, and_3_out, and_5_out, and_6_out, and_7_out, and_8_out, b_bit, clk_t, mul,
       mult_done, mult_start, multiplexer_2_out, or_1_out, or_2_out, or_5_out, step1, step1_done, STEP_q,
       step_we, we;
  wire [4:0] adder_1_out, ITER_q, multiplexer_1_out;
  wire [31:0] bit_extender_1_out, bit_extender_2_out, multiplexer_3_out, multiplexer_4_out, multiplexer_5_out;
  wire [63:0] mul_double_add_32_1_outp;

  and and_1 (and_1_out, UNTIL_MULT_DONE, mult_done);
  and and_2 (clk_t, ~and_1_out, CLK);  // AND_Gate
  Multiplexer #(.width(5)) multiplexer_1 (.in0(adder_1_out), .in1({5{1'b0}}), .out(multiplexer_1_out), .sel(START));
  Multiplexer multiplexer_2 (.in0(adder_2_out), .in1(1'b0), .out(multiplexer_2_out), .sel(START));
  Register #(.width(5)) ITER (.D(multiplexer_1_out), .en(we), .clk(clk_t), .Q(ITER_q), .clr(1'b0));
  Register #(.width(1)) STEP (.D(multiplexer_2_out), .en(step_we), .clk(clk_t), .Q(STEP_q), .clr(1'b0));
  and and_3 (and_3_out, mul, ~b_bit);  // AND_Gate
  Multiplexer #(.width(32)) multiplexer_3 (.in0(multiplexer_5_out), .in1(32'h1), .out(multiplexer_3_out), .sel(START));
  Register #(.width(32)) ACC (.D(multiplexer_3_out), .en(we), .clk(clk_t), .Q(OUTP), .clr(1'b0));
  Adder #(.width(5)) adder_1 (.a(5'b00001), .b(ITER_q), .out(adder_1_out));  // open: cin, cout
  Adder #(.width(1)) adder_2 (.a(1'b1), .b(STEP_q), .out(adder_2_out));  // open: cin, cout
  or or_1 (or_1_out, mult_done, and_3_out);
  Comparator #(.width(5)) comparator_1 (.a(ITER_q), .b(5'b00101), .eq(DONE));  // open: gt, lt
  not not_1 (mul, ITER_q[0]);
  Decoder #(.enable("false")) decoder_1 (.out0(mult_start), .out1(step1), .sel(STEP_q));
  and and_4 (step1_done, step1, or_1_out);
  assign bit_extender_1_out = {{28{1'b0}}, A};  // Bit_Extender bit_extender_1
  Multiplexer #(.width(32)) multiplexer_4 (.in0(OUTP), .in1(bit_extender_1_out), .out(multiplexer_4_out), .sel(mul));
  and and_5 (and_5_out, ~DONE, step1_done);  // AND_Gate
  or or_2 (or_2_out, mult_start, step1_done);
  mul_double_add_32 mul_double_add_32_1 (
    .A(OUTP), .B(multiplexer_4_out), .CLK(clk_t), .START(mult_start), .OUTP(mul_double_add_32_1_outp),
    .DONE(mult_done));
  and and_6 (and_6_out, ~START, and_7_out);  // AND_Gate
  and and_7 (and_7_out, mul, we);
  or or_3 (we, START, and_5_out);
  or or_4 (step_we, START, and_8_out);
  and and_8 (and_8_out, ~DONE, or_2_out);  // AND_Gate
  Bit_Extender #(.in_width(64), .out_width(32), .\type ("zero")) bit_extender_2 (
    .in(mul_double_add_32_1_outp), .out(bit_extender_2_out));
  // Shift_Register #(.length(3)) shift_register_1: pin names not known; wires that end beside it: 1'b0, START, and_6_out, clk_t, 1'b0, B[0], B[1], B[2], b_bit
  // Probe on multiplexer_5_out
  Multiplexer #(.width(32)) multiplexer_5 (
    .in0(OUTP), .in1(bit_extender_2_out), .out(multiplexer_5_out), .sel(or_5_out));
  or or_5 (or_5_out, ~mul, b_bit);  // OR_Gate

  // Other names for the same wires on the sheet: step0 = mult_start

  // Notes on the sheet:
  //   step1 done if:
  //   - mult_done (square or multiply)
  //   - multiply and it would be ignored
endmodule

module demo (
  input  [3:0] A,
  input  [2:0] B
);

  wire button_1_out, clock_1_out, clock_2_out, comparator_1_eq, done, not_1_out;
  wire [11:0] counter_1_q;
  wire [31:0] sq_mul_sekvmul_5_1_outp;

  Button button_1 (.out(button_1_out));
  Counter #(.max('hfff), .width(12)) counter_1 (
    .clr(button_1_out), .load(1'b0), .up(1'b1), .count(not_1_out), .clk(clock_1_out), .Q(counter_1_q));  // open: D, carry
  not not_1 (not_1_out, done);
  Clock clock_1 (.out(clock_1_out));
  Comparator #(.width(12)) comparator_1 (.a({12{1'b0}}), .b(counter_1_q), .eq(comparator_1_eq));  // open: gt, lt
  Clock clock_2 (.out(clock_2_out));
  _7_Segment_Display u_7_segment_display_1 ();  // open: g, f, a, b, e, d, c, dp
  // BCD_to_7_Segment_decoder bcd_to_7_segment_decoder_1: pin names not known
  // Binary_to_BCD_converter #(.binvalue(12)) binary_to_bcd_converter_1: pin names not known; wires that end beside it: counter_1_q
  _7_Segment_Display u_7_segment_display_2 ();  // open: g, f, a, b, e, d, c, dp
  // BCD_to_7_Segment_decoder bcd_to_7_segment_decoder_2: pin names not known
  // Probe on sq_mul_sekvmul_5_1_outp
  _7_Segment_Display u_7_segment_display_3 ();  // open: g, f, a, b, e, d, c, dp
  _7_Segment_Display u_7_segment_display_4 ();  // open: g, f, a, b, e, d, c, dp
  // BCD_to_7_Segment_decoder bcd_to_7_segment_decoder_3: pin names not known
  // BCD_to_7_Segment_decoder bcd_to_7_segment_decoder_4: pin names not known
  sq_mul_sekvmul_5 sq_mul_sekvmul_5_1 (
    .A(A), .UNTIL_MULT_DONE(1'b0), .B(B), .CLK(clock_2_out), .START(comparator_1_eq),
    .OUTP(sq_mul_sekvmul_5_1_outp), .DONE(done));
  LED led_1 (.in(done));
endmodule
